// Digital circuit HW-Q19.dig as structural Verilog
module HW_Q19 (
  input  in_A,
  input  in_B,
  output out
);

  wire A, nfet_1_s, pfet_1_d;

  not not_1 (A, in_A);
  PFET pfet_1 (.G(A), .S(1'b1), .D(pfet_1_d));
  PFET pfet_2 (.G(in_B), .S(1'b1), .D(pfet_1_d));
  NFET nfet_1 (.G(A), .D(pfet_1_d), .S(nfet_1_s));
  NFET nfet_2 (.G(in_B), .D(nfet_1_s), .S(1'b0));
  PFET pfet_3 (.G(pfet_1_d), .S(1'b1), .D(out));
  NFET nfet_3 (.G(pfet_1_d), .D(out), .S(1'b0));

  // Other names for the same wires on the sheet: B = in_B
endmodule
