// Digital circuit part_a.dig as structural Verilog
module part_a (
  input  in_0,
  input  in_1,
  input  in_2,
  output out_0
);

  wire and_1_out, not_1_out;

  and and_1 (and_1_out, in_0, not_1_out);
  not not_1 (not_1_out, in_1);
  or or_1 (out_0, and_1_out, in_2);
endmodule

/* Test case part_a_test:
in_0 in_1 in_2 out_0
 0     0    0     0
 0     0    1     1
 0     1    0     0
 0     1    1     1
 1     0    0     1
 1     0    1     1
 1     1    0     0
 1     1    1     1
*/
